// Logisim project CRC_verify.circ as structural Verilog: 2 circuits, main circuit 4bit_mod2
module _4bit_mod2 (
  input  [3:0] A,
  input  [3:0] B,
  output [2:0] C,
  output out_4
);

  wire [3:0] xor_1_out;

  assign xor_1_out = A ^ B;  // XOR_Gate xor_1, 4 bits wide
  // Probe on xor_1_out[2:0]
  Multiplexer #(.width(3)) multiplexer_1 (.in0(A[2:0]), .in1(xor_1_out[2:0]), .out(C), .sel(A[3]));  // open: en

  assign out_4 = A[3];
endmodule

module CRC (
  input  [7:0] inA,
  input  [3:0] inB,
  output [10:0] C
);

  wire [2:0] n4bit_mod2_1_c, n4bit_mod2_2_c, n4bit_mod2_3_c, n4bit_mod2_4_c, n4bit_mod2_5_c, n4bit_mod2_7_c;
  wire [3:1] n4bit_mod2_6_c;

  // Probe on inA[7:4]
  _4bit_mod2 u_4bit_mod2_1 (.A(inA[7:4]), .B(inB), .C(n4bit_mod2_1_c));  // open: out_4
  // Probe on n4bit_mod2_1_c
  // Probe on {n4bit_mod2_1_c, inA[3]}
  _4bit_mod2 u_4bit_mod2_2 (.A({n4bit_mod2_1_c, inA[3]}), .B(inB), .C(n4bit_mod2_2_c));  // open: out_4
  // Probe on n4bit_mod2_2_c
  // Probe on {n4bit_mod2_2_c, inA[2]}
  _4bit_mod2 u_4bit_mod2_3 (.A({n4bit_mod2_2_c, inA[2]}), .B(inB), .C(n4bit_mod2_3_c));  // open: out_4
  // Probe on n4bit_mod2_3_c
  _4bit_mod2 u_4bit_mod2_4 (.A({n4bit_mod2_3_c, inA[1]}), .B(inB), .C(n4bit_mod2_4_c));  // open: out_4
  // Probe on n4bit_mod2_4_c
  _4bit_mod2 u_4bit_mod2_5 (.A({n4bit_mod2_4_c, inA[0]}), .B(inB), .C(n4bit_mod2_5_c));  // open: out_4
  // Probe on n4bit_mod2_5_c
  _4bit_mod2 u_4bit_mod2_6 (.A({n4bit_mod2_5_c, 1'b0}), .B(inB), .C(n4bit_mod2_6_c));  // open: out_4
  _4bit_mod2 u_4bit_mod2_7 (.A({n4bit_mod2_6_c, 1'b0}), .B(inB), .C(n4bit_mod2_7_c));  // open: out_4
  _4bit_mod2 u_4bit_mod2_8 (.A({n4bit_mod2_7_c, 1'b0}), .B(inB), .C(C[2:0]));  // open: out_4

  assign C[10:3] = inA;

  // Other names for the same wires on the sheet: crc[2:0] = C[2:0]; A[7:0] = inA
endmodule
