// Logisim project FSM.circ as structural Verilog: 1 circuit, main circuit fsm
module fsm (
  input  CLR,
  input  [1:0] in,
  output Z
);

  wire and_1_out, and_2_out, and_3_out, and_4_out, and_5_out, and_6_out, clock_1_out, decoder_1_out0,
       decoder_1_out1, decoder_1_out2, decoder_1_out3, decoder_1_out4, not_1_out, not_2_out, not_3_out,
       not_4_out, not_5_out, or_1_out, or_2_out, or_3_out, or_4_out, or_5_out;
  wire [2:0] multiplexer_1_out, priority_encoder_1_out, state;

  Decoder #(.select(3)) decoder_1 (
    .out0(decoder_1_out0), .out1(decoder_1_out1), .out2(decoder_1_out2), .out3(decoder_1_out3),
    .out4(decoder_1_out4), .sel(state));  // open: out5, out6, out7, en
  or or_1 (or_1_out, decoder_1_out0, decoder_1_out4);
  not not_1 (not_1_out, in[0]);
  or or_2 (or_2_out, decoder_1_out0, decoder_1_out3, decoder_1_out4);
  not not_2 (not_2_out, in[1]);
  or or_3 (or_3_out, decoder_1_out1, decoder_1_out2);
  not not_3 (not_3_out, in[1]);
  or or_4 (or_4_out, decoder_1_out1, decoder_1_out2);
  not not_4 (not_4_out, in[0]);
  not not_5 (not_5_out, in[0]);
  and and_1 (and_1_out, in[1], in[0]);
  and and_2 (and_2_out, or_1_out, not_1_out);
  and and_3 (and_3_out, or_2_out, not_2_out, in[0]);
  and and_4 (and_4_out, or_3_out, not_3_out, in[0]);
  and and_5 (and_5_out, or_4_out, not_4_out);
  and and_6 (and_6_out, decoder_1_out3, not_5_out);
  or or_5 (or_5_out, and_1_out, and_2_out);
  Clock clock_1 (.out(clock_1_out));
  Priority_Encoder priority_encoder_1 (
    .in0(or_5_out), .in1(and_3_out), .in2(and_4_out), .in3(and_5_out), .in4(and_6_out), .in5(1'b0),
    .in6(1'b0), .in7(1'b0), .out(priority_encoder_1_out));  // open: en_in, gs, en_out
  Multiplexer #(.width(3)) multiplexer_1 (
    .in0(priority_encoder_1_out), .in1(3'b000), .out(multiplexer_1_out), .sel(CLR));  // open: en
  Register #(.width(3)) register_1 (.D(multiplexer_1_out), .Q(state), .clk(clock_1_out));  // open: en, clr
  Comparator #(.width(3), .mode("unsigned")) comparator_1 (
    .a(priority_encoder_1_out), .b(3'b100), .eq(Z));  // open: gt, lt
endmodule
