// Logisim project GRF.circ as structural Verilog: 2 circuits, main circuit grf
module grf (
  input  clk,
  input  reset,
  input  WE,
  input  [4:0] A1,
  input  [4:0] A2,
  input  [4:0] A3,
  input  [31:0] WD,
  output [31:0] RD1,
  output [31:0] RD2
);

  wire comparator_1_eq, in1, in2, in3, in4, in5, in6, in7, in8, in9, in10, in11, in12, in13, in14, in15,
       in16, in17, in18, in19, in20, in21, in22, in23, in24, in25, in26, in27, in28, in29, in30, in31, in32;
  wire [31:0] in, o1, o2, o3, o4, o5, o6, o7, o8, o9, o10, o11, o12, o13, o14, o15, o16, o17, o18, o19, o20,
       o21, o22, o23, o24, o25, o26, o27, o28, o29, o30, o31, o32;

  Demultiplexer #(.select(5)) demultiplexer_1 (
    .out0(in1), .out1(in2), .out2(in3), .out3(in4), .out4(in5), .out5(in6), .out6(in7), .out7(in8),
    .out8(in9), .out9(in10), .out10(in11), .out11(in12), .out12(in13), .out13(in14), .out14(in15),
    .out15(in16), .out16(in17), .out17(in18), .out18(in19), .out19(in20), .out20(in21), .out21(in22),
    .out22(in23), .out23(in24), .out24(in25), .out25(in26), .out26(in27), .out27(in28), .out28(in29),
    .out29(in30), .out30(in31), .out31(in32), .in(WE), .sel(A3));  // open: en
  Comparator #(.width(5)) comparator_1 (.a(A3), .b({5{1'b0}}), .eq(comparator_1_eq));  // open: gt, lt
  Multiplexer #(.width(32), .disabled(0)) multiplexer_1 (
    .in0(WD), .in1({32{1'b0}}), .out(in), .sel(comparator_1_eq));  // open: en
  Multiplexer #(.select(5), .width(32)) multiplexer_2 (
    .in0(o1), .in1(o2), .in2(o3), .in3(o4), .in4(o5), .in5(o6), .in6(o7), .in7(o8), .in8(o9), .in9(o10),
    .in10(o11), .in11(o12), .in12(o13), .in13(o14), .in14(o15), .in15(o16), .in16(o17), .in17(o18),
    .in18(o19), .in19(o20), .in20(o21), .in21(o22), .in22(o23), .in23(o24), .in24(o25), .in25(o26),
    .in26(o27), .in27(o28), .in28(o29), .in29(o30), .in30(o31), .in31(o32), .out(RD1), .sel(A1));  // open: en
  Multiplexer #(.select(5), .width(32)) multiplexer_3 (
    .in0(o1), .in1(o2), .in2(o3), .in3(o4), .in4(o5), .in5(o6), .in6(o7), .in7(o8), .in8(o9), .in9(o10),
    .in10(o11), .in11(o12), .in12(o13), .in13(o14), .in14(o15), .in15(o16), .in16(o17), .in17(o18),
    .in18(o19), .in19(o20), .in20(o21), .in21(o22), .in22(o23), .in23(o24), .in24(o25), .in25(o26),
    .in26(o27), .in27(o28), .in28(o29), .in29(o30), .in30(o31), .in31(o32), .out(RD2), .sel(A2));  // open: en
  Register #(.width(32)) register_1 (.D(in), .en(in1), .Q(o1), .clk(clk), .clr(reset));
  Register #(.width(32)) register_2 (.D(in), .en(in9), .Q(o9), .clk(clk), .clr(reset));
  Register #(.width(32)) register_3 (.D(in), .en(in17), .Q(o17), .clk(clk), .clr(reset));
  Register #(.width(32)) register_4 (.D(in), .en(in25), .Q(o25), .clk(clk), .clr(reset));
  // Probe on in
  Register #(.width(32)) register_5 (.D(in), .en(in2), .Q(o2), .clk(clk), .clr(reset));
  Register #(.width(32)) register_6 (.D(in), .en(in10), .Q(o10), .clk(clk), .clr(reset));
  Register #(.width(32)) register_7 (.D(in), .en(in18), .Q(o18), .clk(clk), .clr(reset));
  Register #(.width(32)) register_8 (.D(in), .en(in26), .Q(o26), .clk(clk), .clr(reset));
  Register #(.width(32)) register_9 (.D(in), .en(in3), .Q(o3), .clk(clk), .clr(reset));
  Register #(.width(32)) register_10 (.D(in), .en(in11), .Q(o11), .clk(clk), .clr(reset));
  Register #(.width(32)) register_11 (.D(in), .en(in19), .Q(o19), .clk(clk), .clr(reset));
  Register #(.width(32)) register_12 (.D(in), .en(in27), .Q(o27), .clk(clk), .clr(reset));
  // Probe on o3
  Register #(.width(32)) register_13 (.D(in), .en(in4), .Q(o4), .clk(clk), .clr(reset));
  Register #(.width(32)) register_14 (.D(in), .en(in12), .Q(o12), .clk(clk), .clr(reset));
  Register #(.width(32)) register_15 (.D(in), .en(in20), .Q(o20), .clk(clk), .clr(reset));
  Register #(.width(32)) register_16 (.D(in), .en(in28), .Q(o28), .clk(clk), .clr(reset));
  Register #(.width(32)) register_17 (.D(in), .en(in5), .Q(o5), .clk(clk), .clr(reset));
  Register #(.width(32)) register_18 (.D(in), .en(in13), .Q(o13), .clk(clk), .clr(reset));
  Register #(.width(32)) register_19 (.D(in), .en(in21), .Q(o21), .clk(clk), .clr(reset));
  Register #(.width(32)) register_20 (.D(in), .en(in29), .Q(o29), .clk(clk), .clr(reset));
  Register #(.width(32)) register_21 (.D(in), .en(in6), .Q(o6), .clk(clk), .clr(reset));
  Register #(.width(32)) register_22 (.D(in), .en(in14), .Q(o14), .clk(clk), .clr(reset));
  Register #(.width(32)) register_23 (.D(in), .en(in22), .Q(o22), .clk(clk), .clr(reset));
  Register #(.width(32)) register_24 (.D(in), .en(in30), .Q(o30), .clk(clk), .clr(reset));
  Register #(.width(32)) register_25 (.D(in), .en(in7), .Q(o7), .clk(clk), .clr(reset));
  Register #(.width(32)) register_26 (.D(in), .en(in15), .Q(o15), .clk(clk), .clr(reset));
  Register #(.width(32)) register_27 (.D(in), .en(in23), .Q(o23), .clk(clk), .clr(reset));
  Register #(.width(32)) register_28 (.D(in), .en(in31), .Q(o31), .clk(clk), .clr(reset));
  Register #(.width(32)) register_29 (.D(in), .en(in8), .Q(o8), .clk(clk), .clr(reset));
  Register #(.width(32)) register_30 (.D(in), .en(in16), .Q(o16), .clk(clk), .clr(reset));
  Register #(.width(32)) register_31 (.D(in), .en(in24), .Q(o24), .clk(clk), .clr(reset));
  Register #(.width(32)) register_32 (.D(in), .en(in32), .Q(o32), .clk(clk), .clr(reset));
endmodule

module t (
  input  in_1
);

  wire in1, in2, in3, in4, in5, in6, in7, in8, in9, in10, in11, in12, in13, in14, in15, in16, in17, in18,
       in19, in20, in21, in22, in23, in24, in25, in26, in27, in28, in29, in30, in31, in32;
  wire [4:0] A3;

  Demultiplexer #(.select(5)) demultiplexer_1 (
    .out0(in1), .out1(in2), .out2(in3), .out3(in4), .out4(in5), .out5(in6), .out6(in7), .out7(in8),
    .out8(in9), .out9(in10), .out10(in11), .out11(in12), .out12(in13), .out13(in14), .out14(in15),
    .out15(in16), .out16(in17), .out17(in18), .out18(in19), .out19(in20), .out20(in21), .out21(in22),
    .out22(in23), .out23(in24), .out24(in25), .out25(in26), .out26(in27), .out27(in28), .out28(in29),
    .out29(in30), .out30(in31), .out31(in32), .in(in_1), .sel(A3));  // open: en
endmodule
