// Logisim project ftoi.circ as structural Verilog: 2 circuits, main circuit ftoi
module ftoi (
  input  [15:0] float,
  output [31:0] \int 
);

  wire and_1_out, and_2_out, and_3_out, denormal, E_equal_zero, E_less_zero, inf_or_nan, not_1_out,
       not_2_out, or_1_out, out_zero, subtractor_2_bout;
  wire [4:0] E, r_shift, subtractor_2_out, subtractor_3_out;
  wire [31:0] adder_1_out, bit_extender_1_out, int_t, multiplexer_1_out, multiplexer_2_out, or_3_out,
       shifter_1_out, shifter_2_out, shifter_3_out, xor_2_out;

  // Probe on float[14:10]
  or or_1 (or_1_out, E_less_zero, E_equal_zero);
  // Probe on E
  Subtractor #(.width(5)) subtractor_1 (.a(float[14:10]), .b(5'b01111), .out(E), .bout(E_less_zero));  // open: bin
  Comparator #(.width(5), .mode("unsigned")) comparator_1 (
    .a(float[14:10]), .b({5{1'b1}}), .eq(inf_or_nan));  // open: gt, lt
  Comparator #(.width(5), .mode("unsigned")) comparator_2 (
    .a(float[14:10]), .b({5{1'b0}}), .eq(denormal));  // open: gt, lt
  not not_1 (not_1_out, denormal);
  and and_1 (and_1_out, not_1_out, not_2_out);
  not not_2 (not_2_out, inf_or_nan);
  and and_2 (and_2_out, denormal, or_1_out);
  Comparator #(.width(5), .mode("unsigned")) comparator_3 (.a(E), .b({5{1'b0}}), .eq(E_equal_zero));  // open: gt, lt
  and and_3 (and_3_out, E_less_zero, and_1_out);
  or or_2 (out_zero, inf_or_nan, and_3_out, and_2_out);
  Multiplexer #(.width(32)) multiplexer_1 (
    .in0(32'h1), .in1({32{1'b0}}), .out(multiplexer_1_out), .sel(denormal));  // open: en
  // Probe on bit_extender_1_out
  assign bit_extender_1_out = {{22{1'b0}}, float[9:0]};  // Bit_Extender bit_extender_1
  Subtractor #(.width(5)) subtractor_2 (
    .a(E), .b(5'b01010), .out(subtractor_2_out), .bout(subtractor_2_bout));  // open: bin
  // Probe on subtractor_2_out
  Shifter #(.width(32)) shifter_1 (.in(multiplexer_1_out), .\dist (E), .out(shifter_1_out));
  Shifter #(.width(32)) shifter_2 (.in(bit_extender_1_out), .\dist (subtractor_2_out), .out(shifter_2_out));
  Shifter #(.width(32), .shift("lr")) shifter_3 (.in(bit_extender_1_out), .\dist (r_shift), .out(shifter_3_out));
  // Probe on shifter_3_out
  Multiplexer #(.width(32)) multiplexer_2 (
    .in0(shifter_2_out), .in1(shifter_3_out), .out(multiplexer_2_out), .sel(subtractor_2_bout));  // open: en
  // Probe on subtractor_3_out
  Subtractor #(.width(5)) subtractor_3 (.a(subtractor_2_out), .b(5'b00001), .out(subtractor_3_out));  // open: bin, bout
  assign or_3_out = shifter_1_out | multiplexer_2_out;  // OR_Gate or_3, 32 bits wide
  // Probe on xor_2_out
  // Probe on r_shift
  assign r_shift = subtractor_3_out ^ {5{1'b1}};  // XOR_Gate xor_1, 5 bits wide
  Multiplexer #(.width(32)) multiplexer_3 (.in0(int_t), .in1({32{1'b0}}), .out(\int ), .sel(out_zero));  // open: en
  assign xor_2_out = or_3_out ^ {32{1'b1}};  // XOR_Gate xor_2, 32 bits wide
  Adder #(.width(32)) adder_1 (.a(xor_2_out), .b(32'h1), .out(adder_1_out));  // open: cin, cout
  Multiplexer #(.width(32)) multiplexer_4 (
    .in0(or_3_out), .in1(adder_1_out), .out(int_t), .sel(float[15]));  // open: en

  // Other names for the same wires on the sheet: fraction[9:0] = float[9:0]; exponent[4:0] = float[14:10];
  //   s = float[15]
endmodule

module \new  (
  input  [31:0] in_1,
  input  [4:0] in_2,
  input  [4:0] in_3,
  input  [31:0] in_4,
  output [31:0] out_5
);

  wire [4:0] E, exponent, subtractor_1_out, subtractor_2_out;
  wire [31:0] subtractor_3_out, xor_2_out;

  // Probe on exponent
  // Probe on subtractor_1_out
  Subtractor #(.width(5)) subtractor_1 (.a(exponent), .b(5'b01111), .out(subtractor_1_out));  // open: bin, bout
  // Probe on subtractor_2_out
  Subtractor #(.width(5)) subtractor_2 (.a(in_3), .b(5'b00001), .out(subtractor_2_out));  // open: bin, bout
  Subtractor #(.width(32)) subtractor_3 (.a(in_4), .b(32'h1), .out(subtractor_3_out));  // open: bin, bout
  // Probe on E
  assign E = subtractor_2_out ^ {5{1'b1}};  // XOR_Gate xor_1, 5 bits wide
  Shifter #(.width(32), .shift("lr")) shifter_1 (.in(in_1), .\dist (in_2), .out(out_5));
  // Probe on xor_2_out
  assign xor_2_out = subtractor_3_out ^ {32{1'b1}};  // XOR_Gate xor_2, 32 bits wide
endmodule
