// Logisim project navigation.circ as structural Verilog: 4 circuits, main circuit navigation
module navigation (
  input  [1:0] dir,
  input  in_2,
  input  reset,
  output arrive,
  output hit
);

  wire and_1_out, and_2_out, and_3_out, and_4_out, and_5_out, and_6_out, and_7_out, and_8_out, and_9_out,
       and_10_out, and_11_out, and_12_out, and_13_out, and_14_out, and_15_out, and_16_out, and_17_out,
       and_18_out, and_19_out, and_20_out, and_21_out, and_22_out, and_23_out, and_24_out, and_25_out,
       and_26_out, and_27_out, and_28_out, comparator_1_gt, not_1_out, not_2_out, not_3_out, not_4_out,
       not_5_out, not_6_out, not_7_out, not_8_out, not_9_out, not_10_out, not_11_out, not_12_out, not_13_out,
       not_14_out, not_15_out, not_16_out, not_17_out, not_18_out, not_19_out, not_20_out, not_21_out,
       not_22_out, not_23_out, not_24_out, not_25_out, not_26_out, not_27_out, not_28_out, not_29_out,
       not_30_out, not_31_out, not_32_out, not_33_out, not_34_out, not_35_out, not_36_out, not_37_out,
       not_38_out, not_39_out, not_40_out, not_41_out, not_42_out, not_43_out, not_44_out, not_45_out,
       not_46_out, not_47_out, not_48_out, not_49_out, not_50_out, not_51_out, not_52_out, not_53_out,
       not_54_out, not_55_out, not_56_out, not_57_out, not_58_out, not_59_out, not_60_out, not_61_out,
       not_62_out, not_63_out, not_64_out, not_65_out, not_66_out, now0, now1, now2, now3, state0, state1,
       state2, state3;

  not not_1 (not_1_out, state3);
  not not_2 (not_2_out, state2);
  not not_3 (not_3_out, state0);
  not not_4 (not_4_out, dir[1]);
  not not_5 (not_5_out, state3);
  not not_6 (not_6_out, state2);
  not not_7 (not_7_out, state0);
  not not_8 (not_8_out, dir[0]);
  not not_9 (not_9_out, state2);
  not not_10 (not_10_out, state1);
  not not_11 (not_11_out, state0);
  not not_12 (not_12_out, dir[1]);
  not not_13 (not_13_out, state2);
  not not_14 (not_14_out, state1);
  not not_15 (not_15_out, state0);
  not not_16 (not_16_out, dir[0]);
  not not_17 (not_17_out, state2);
  not not_18 (not_18_out, state1);
  not not_19 (not_19_out, dir[1]);
  not not_20 (not_20_out, dir[0]);
  not not_21 (not_21_out, state3);
  not not_22 (not_22_out, state2);
  not not_23 (not_23_out, state1);
  not not_24 (not_24_out, state0);
  not not_25 (not_25_out, state3);
  not not_26 (not_26_out, state2);
  not not_27 (not_27_out, state1);
  not not_28 (not_28_out, state0);
  not not_29 (not_29_out, state3);
  not not_30 (not_30_out, state1);
  not not_31 (not_31_out, state1);
  not not_32 (not_32_out, dir[1]);
  not not_33 (not_33_out, dir[0]);
  not not_34 (not_34_out, state1);
  not not_35 (not_35_out, dir[1]);
  not not_36 (not_36_out, dir[0]);
  not not_37 (not_37_out, dir[1]);
  not not_38 (not_38_out, dir[0]);
  not not_39 (not_39_out, state0);
  not not_40 (not_40_out, state0);
  not not_41 (not_41_out, state3);
  not not_42 (not_42_out, state2);
  not not_43 (not_43_out, state1);
  not not_44 (not_44_out, state3);
  not not_45 (not_45_out, state1);
  not not_46 (not_46_out, dir[1]);
  not not_47 (not_47_out, state3);
  not not_48 (not_48_out, state2);
  not not_49 (not_49_out, state1);
  not not_50 (not_50_out, state0);
  not not_51 (not_51_out, state2);
  not not_52 (not_52_out, state0);
  not not_53 (not_53_out, dir[1]);
  not not_54 (not_54_out, dir[0]);
  not not_55 (not_55_out, state0);
  not not_56 (not_56_out, dir[1]);
  not not_57 (not_57_out, dir[0]);
  not not_58 (not_58_out, state0);
  not not_59 (not_59_out, dir[1]);
  not not_60 (not_60_out, dir[0]);
  not not_61 (not_61_out, state1);
  not not_62 (not_62_out, state2);
  not not_63 (not_63_out, state0);
  not not_64 (not_64_out, state1);
  and and_1 (and_1_out, not_1_out, not_2_out, state1, not_3_out, not_4_out, dir[0]);
  and and_2 (and_2_out, not_5_out, not_6_out, state1, not_7_out, dir[1], not_8_out);
  and and_3 (and_3_out, state3, not_9_out, not_10_out, not_11_out, not_12_out, dir[0]);
  and and_4 (and_4_out, state3, not_13_out, not_14_out, not_15_out, dir[1], not_16_out);
  and and_5 (and_5_out, state3, not_17_out, not_18_out, state0, not_19_out, not_20_out);
  and and_6 (and_6_out, not_21_out, not_22_out, not_23_out, not_24_out, dir[0]);
  and and_7 (and_7_out, not_25_out, not_26_out, not_27_out, not_28_out, dir[1]);
  and and_8 (and_8_out, not_29_out, not_30_out, dir[1], dir[0]);
  and and_9 (and_9_out, not_31_out, state0, not_32_out, not_33_out);
  and and_10 (and_10_out, state2, not_34_out, not_35_out, not_36_out);
  and and_11 (and_11_out, state2, dir[1], dir[0]);
  and and_12 (and_12_out, state2, state0, not_37_out, not_38_out);
  and and_13 (and_13_out, state2, state1, not_39_out, dir[0]);
  and and_14 (and_14_out, state2, state1, not_40_out, dir[1]);
  and and_15 (and_15_out, not_41_out, not_42_out, not_43_out, dir[0]);
  and and_16 (and_16_out, not_44_out, not_45_out, not_46_out, dir[0]);
  and and_17 (and_17_out, not_47_out, not_48_out, not_49_out, not_50_out, dir[1]);
  and and_18 (and_18_out, not_51_out, state1, not_52_out, not_53_out, not_54_out);
  and and_19 (and_19_out, state2, state1, dir[0]);
  and and_20 (and_20_out, state2, state1, not_55_out, dir[1]);
  and and_21 (and_21_out, state3, not_56_out, not_57_out);
  and and_22 (and_22_out, not_58_out, not_59_out, not_60_out);
  and and_23 (and_23_out, not_61_out, state0, dir[1], dir[0]);
  and and_24 (and_24_out, not_62_out, state1, not_63_out, dir[1], dir[0]);
  and and_25 (and_25_out, state2, not_64_out);
  and and_26 (and_26_out, state2, state0, dir[1], dir[0]);
  and and_27 (and_27_out, state3, dir[1], dir[0]);
  or or_1 (now3, and_1_out, and_2_out, and_3_out, and_4_out, and_5_out);
  or or_2 (now2, and_6_out, and_7_out, and_8_out, and_9_out, and_10_out, and_11_out, and_12_out, and_13_out, and_14_out);
  or or_3 (now1, and_15_out, and_16_out, and_17_out, and_18_out, and_19_out, and_20_out, and_21_out);
  or or_4 (now0, and_22_out, and_23_out, and_24_out, and_25_out, and_26_out, and_27_out);
  Register #(.width(1)) register_1 (.D(now3), .Q(state3), .clk(in_2), .clr(reset));  // open: en
  Register #(.width(1)) register_2 (.D(now2), .Q(state2), .clk(in_2), .clr(reset));  // open: en
  Register #(.width(1)) register_3 (.D(now1), .Q(state1), .clk(in_2), .clr(reset));  // open: en
  Register #(.width(1)) register_4 (.D(now0), .Q(state0), .clk(in_2), .clr(reset));  // open: en
  // Probe on state3
  // Probe on state2
  // Probe on state1
  // Probe on state0
  not not_65 (not_65_out, state3);
  not not_66 (not_66_out, state2);
  and and_28 (and_28_out, not_65_out, not_66_out, state1, state0);
  Comparator #(.width(4), .mode("unsigned")) comparator_1 (
    .a({state3, state2, state1, state0}), .b(4'b0100), .gt(comparator_1_gt));  // open: eq, lt
  // Probe on {state3, state2, state1, state0}
  Multiplexer multiplexer_1 (.in0(and_28_out), .in1(1'b0), .out(arrive), .sel(reset));  // open: en
  Multiplexer multiplexer_2 (.in0(comparator_1_gt), .in1(1'b0), .out(hit), .sel(reset));  // open: en

  // Other names for the same wires on the sheet: clk = in_2
endmodule

module test (
  input  in_1,
  input  in_2,
  output out_3,
  output [3:0] out_4,
  output out_5,
  output out_6,
  output out_7,
  output [3:0] out_8,
  output out_9,
  output out_10
);

  wire clock_1_out, clock_2_out;
  wire [1:0] rom_1_data, rom_2_data;
  wire [4:0] counter_1_q, counter_2_q;

  Clock clock_1 (.out(clock_1_out));
  Counter #(.width(5), .max('h1f)) counter_1 (
    .Q(counter_1_q), .carry(out_6), .clk(clock_2_out), .clr(in_1));  // open: load, D, count
  Clock clock_2 (.out(clock_2_out));
  Counter #(.width(5), .max('h1f)) counter_2 (
    .Q(counter_2_q), .carry(out_10), .clk(clock_1_out), .clr(in_2));  // open: load, D, count
  ROM #(.addrWidth(5), .dataWidth(2)) rom_1 (.addr(counter_1_q), .data(rom_1_data));  // open: sel
  ROM #(.addrWidth(5), .dataWidth(2)) rom_2 (.addr(counter_2_q), .data(rom_2_data));  // open: sel
  navigation navigation_1 (.dir(rom_1_data), .in_2(clock_2_out), .reset(out_6), .arrive(out_3), .hit(out_5));
  nav1 nav1_1 (.dir(rom_2_data), .in_2(clock_1_out), .reset(in_2), .arrive(out_7), .out_5(out_8), .hit(out_9));

  // Notes on the sheet:
  //   contents of rom_1 (hex, n*v repeats v):
  //   0 3 0 4*3 1 1 2 0 0 2 3 1 2 3 1 2 3 2 2 0 2 1 0 3 3 2 0 0 3
  //   contents of rom_2 (hex, n*v repeats v):
  //   0 1 0 1 0 1 3 0 1 2 0 0 2 3 1 2 3 1 2 3 2 2 0 2 1 0 3 3 2 0 0 3
endmodule

module \new  (
  input  s3,
  input  s2,
  input  s1,
  input  s0,
  input  in_high,
  input  in_low,
  output s3_2,
  output s2_2,
  output s1_2,
  output s0_2
);

  wire and_1_out, and_2_out, and_3_out, and_4_out, and_5_out, and_6_out, and_7_out, and_8_out, and_9_out,
       and_10_out, and_11_out, and_12_out, and_13_out, and_14_out, and_15_out, and_16_out, and_17_out,
       and_18_out, and_19_out, and_20_out, and_21_out, and_22_out, and_23_out, and_24_out, and_25_out,
       and_26_out, and_27_out, not_1_out, not_2_out, not_3_out, not_4_out, not_5_out, not_6_out, not_7_out,
       not_8_out, not_9_out, not_10_out, not_11_out, not_12_out, not_13_out, not_14_out, not_15_out,
       not_16_out, not_17_out, not_18_out, not_19_out, not_20_out, not_21_out, not_22_out, not_23_out,
       not_24_out, not_25_out, not_26_out, not_27_out, not_28_out, not_29_out, not_30_out, not_31_out,
       not_32_out, not_33_out, not_34_out, not_35_out, not_36_out, not_37_out, not_38_out, not_39_out,
       not_40_out, not_41_out, not_42_out, not_43_out, not_44_out, not_45_out, not_46_out, not_47_out,
       not_48_out, not_49_out, not_50_out, not_51_out, not_52_out, not_53_out, not_54_out, not_55_out,
       not_56_out, not_57_out, not_58_out, not_59_out, not_60_out, not_61_out, not_62_out, not_63_out,
       not_64_out;

  not not_1 (not_1_out, s3);
  not not_2 (not_2_out, s2);
  not not_3 (not_3_out, s0);
  not not_4 (not_4_out, in_high);
  not not_5 (not_5_out, s3);
  not not_6 (not_6_out, s2);
  not not_7 (not_7_out, s0);
  not not_8 (not_8_out, in_low);
  not not_9 (not_9_out, s2);
  not not_10 (not_10_out, s1);
  not not_11 (not_11_out, s0);
  not not_12 (not_12_out, in_high);
  not not_13 (not_13_out, s2);
  not not_14 (not_14_out, s1);
  not not_15 (not_15_out, s0);
  not not_16 (not_16_out, in_low);
  not not_17 (not_17_out, s2);
  not not_18 (not_18_out, s1);
  not not_19 (not_19_out, in_high);
  not not_20 (not_20_out, in_low);
  not not_21 (not_21_out, s3);
  not not_22 (not_22_out, s2);
  not not_23 (not_23_out, s1);
  not not_24 (not_24_out, s0);
  not not_25 (not_25_out, s3);
  not not_26 (not_26_out, s2);
  not not_27 (not_27_out, s1);
  not not_28 (not_28_out, s0);
  not not_29 (not_29_out, s3);
  not not_30 (not_30_out, s1);
  not not_31 (not_31_out, s1);
  not not_32 (not_32_out, in_high);
  not not_33 (not_33_out, in_low);
  not not_34 (not_34_out, s1);
  not not_35 (not_35_out, in_high);
  not not_36 (not_36_out, in_low);
  not not_37 (not_37_out, in_high);
  not not_38 (not_38_out, in_low);
  not not_39 (not_39_out, s0);
  not not_40 (not_40_out, s0);
  not not_41 (not_41_out, s3);
  not not_42 (not_42_out, s2);
  not not_43 (not_43_out, s1);
  not not_44 (not_44_out, s3);
  not not_45 (not_45_out, s1);
  not not_46 (not_46_out, in_high);
  not not_47 (not_47_out, s3);
  not not_48 (not_48_out, s2);
  not not_49 (not_49_out, s1);
  not not_50 (not_50_out, s0);
  not not_51 (not_51_out, s2);
  not not_52 (not_52_out, s0);
  not not_53 (not_53_out, in_high);
  not not_54 (not_54_out, in_low);
  not not_55 (not_55_out, s0);
  not not_56 (not_56_out, in_high);
  not not_57 (not_57_out, in_low);
  not not_58 (not_58_out, s0);
  not not_59 (not_59_out, in_high);
  not not_60 (not_60_out, in_low);
  not not_61 (not_61_out, s1);
  not not_62 (not_62_out, s2);
  not not_63 (not_63_out, s0);
  not not_64 (not_64_out, s1);
  and and_1 (and_1_out, not_1_out, not_2_out, s1, not_3_out, not_4_out, in_low);
  and and_2 (and_2_out, not_5_out, not_6_out, s1, not_7_out, in_high, not_8_out);
  and and_3 (and_3_out, s3, not_9_out, not_10_out, not_11_out, not_12_out, in_low);
  and and_4 (and_4_out, s3, not_13_out, not_14_out, not_15_out, in_high, not_16_out);
  and and_5 (and_5_out, s3, not_17_out, not_18_out, s0, not_19_out, not_20_out);
  and and_6 (and_6_out, not_21_out, not_22_out, not_23_out, not_24_out, in_low);
  and and_7 (and_7_out, not_25_out, not_26_out, not_27_out, not_28_out, in_high);
  and and_8 (and_8_out, not_29_out, not_30_out, in_high, in_low);
  and and_9 (and_9_out, not_31_out, s0, not_32_out, not_33_out);
  and and_10 (and_10_out, s2, not_34_out, not_35_out, not_36_out);
  and and_11 (and_11_out, s2, in_high, in_low);
  and and_12 (and_12_out, s2, s0, not_37_out, not_38_out);
  and and_13 (and_13_out, s2, s1, not_39_out, in_low);
  and and_14 (and_14_out, s2, s1, not_40_out, in_high);
  and and_15 (and_15_out, not_41_out, not_42_out, not_43_out, in_low);
  and and_16 (and_16_out, not_44_out, not_45_out, not_46_out, in_low);
  and and_17 (and_17_out, not_47_out, not_48_out, not_49_out, not_50_out, in_high);
  and and_18 (and_18_out, not_51_out, s1, not_52_out, not_53_out, not_54_out);
  and and_19 (and_19_out, s2, s1, in_low);
  and and_20 (and_20_out, s2, s1, not_55_out, in_high);
  and and_21 (and_21_out, s3, not_56_out, not_57_out);
  and and_22 (and_22_out, not_58_out, not_59_out, not_60_out);
  and and_23 (and_23_out, not_61_out, s0, in_high, in_low);
  and and_24 (and_24_out, not_62_out, s1, not_63_out, in_high, in_low);
  and and_25 (and_25_out, s2, not_64_out);
  and and_26 (and_26_out, s2, s0, in_high, in_low);
  and and_27 (and_27_out, s3, in_high, in_low);
  or or_1 (s3_2, and_1_out, and_2_out, and_3_out, and_4_out, and_5_out);
  or or_2 (s2_2, and_6_out, and_7_out, and_8_out, and_9_out, and_10_out, and_11_out, and_12_out, and_13_out, and_14_out);
  or or_3 (s1_2, and_15_out, and_16_out, and_17_out, and_18_out, and_19_out, and_20_out, and_21_out);
  or or_4 (s0_2, and_22_out, and_23_out, and_24_out, and_25_out, and_26_out, and_27_out);
endmodule

module nav1 (
  input  [1:0] dir,
  input  in_2,
  input  reset,
  output arrive,
  output [3:0] out_5,
  output hit
);

  wire and_1_out, and_2_out, and_3_out, and_4_out, and_5_out, and_6_out, and_7_out, and_8_out, and_9_out,
       and_10_out, and_11_out, and_12_out, and_13_out, and_14_out, and_15_out, and_16_out, and_17_out,
       and_18_out, and_19_out, and_20_out, and_21_out, and_22_out, and_23_out, and_24_out, and_25_out,
       and_26_out, and_27_out, and_28_out, comparator_1_gt, not_1_out, not_2_out, not_3_out, not_4_out,
       not_5_out, not_6_out, not_7_out, not_8_out, not_9_out, not_10_out, not_11_out, not_12_out, not_13_out,
       not_14_out, not_15_out, not_16_out, not_17_out, not_18_out, not_19_out, not_20_out, not_21_out,
       not_22_out, not_23_out, not_24_out, not_25_out, not_26_out, not_27_out, not_28_out, not_29_out,
       not_30_out, not_31_out, not_32_out, not_33_out, not_34_out, not_35_out, not_36_out, not_37_out,
       not_38_out, not_39_out, not_40_out, not_41_out, not_42_out, not_43_out, not_44_out, not_45_out,
       not_46_out, not_47_out, not_48_out, not_49_out, not_50_out, not_51_out, not_52_out, not_53_out,
       not_54_out, not_55_out, not_56_out, not_57_out, not_58_out, not_59_out, not_60_out, not_61_out,
       not_62_out, not_63_out, not_64_out, not_65_out, not_66_out, state0, state1, state2, state3;

  not not_1 (not_1_out, state3);
  not not_2 (not_2_out, state2);
  not not_3 (not_3_out, state0);
  not not_4 (not_4_out, dir[1]);
  not not_5 (not_5_out, state3);
  not not_6 (not_6_out, state2);
  not not_7 (not_7_out, state0);
  not not_8 (not_8_out, dir[0]);
  not not_9 (not_9_out, state2);
  not not_10 (not_10_out, state1);
  not not_11 (not_11_out, state0);
  not not_12 (not_12_out, dir[1]);
  not not_13 (not_13_out, state2);
  not not_14 (not_14_out, state1);
  not not_15 (not_15_out, state0);
  not not_16 (not_16_out, dir[0]);
  not not_17 (not_17_out, state2);
  not not_18 (not_18_out, state1);
  not not_19 (not_19_out, dir[1]);
  not not_20 (not_20_out, dir[0]);
  not not_21 (not_21_out, state3);
  not not_22 (not_22_out, state2);
  not not_23 (not_23_out, state1);
  not not_24 (not_24_out, state0);
  not not_25 (not_25_out, state3);
  not not_26 (not_26_out, state2);
  not not_27 (not_27_out, state1);
  not not_28 (not_28_out, state0);
  not not_29 (not_29_out, state3);
  not not_30 (not_30_out, state1);
  not not_31 (not_31_out, state1);
  not not_32 (not_32_out, dir[1]);
  not not_33 (not_33_out, dir[0]);
  not not_34 (not_34_out, state1);
  not not_35 (not_35_out, dir[1]);
  not not_36 (not_36_out, dir[0]);
  not not_37 (not_37_out, dir[1]);
  not not_38 (not_38_out, dir[0]);
  not not_39 (not_39_out, state0);
  not not_40 (not_40_out, state0);
  not not_41 (not_41_out, state3);
  not not_42 (not_42_out, state2);
  not not_43 (not_43_out, state1);
  not not_44 (not_44_out, state3);
  not not_45 (not_45_out, state1);
  not not_46 (not_46_out, dir[1]);
  not not_47 (not_47_out, state3);
  not not_48 (not_48_out, state2);
  not not_49 (not_49_out, state1);
  not not_50 (not_50_out, state0);
  not not_51 (not_51_out, state2);
  not not_52 (not_52_out, state0);
  not not_53 (not_53_out, dir[1]);
  not not_54 (not_54_out, dir[0]);
  not not_55 (not_55_out, state0);
  not not_56 (not_56_out, dir[1]);
  not not_57 (not_57_out, dir[0]);
  not not_58 (not_58_out, state0);
  not not_59 (not_59_out, dir[1]);
  not not_60 (not_60_out, dir[0]);
  not not_61 (not_61_out, state1);
  not not_62 (not_62_out, state2);
  not not_63 (not_63_out, state0);
  not not_64 (not_64_out, state1);
  and and_1 (and_1_out, not_1_out, not_2_out, state1, not_3_out, not_4_out, dir[0]);
  and and_2 (and_2_out, not_5_out, not_6_out, state1, not_7_out, dir[1], not_8_out);
  and and_3 (and_3_out, state3, not_9_out, not_10_out, not_11_out, not_12_out, dir[0]);
  and and_4 (and_4_out, state3, not_13_out, not_14_out, not_15_out, dir[1], not_16_out);
  and and_5 (and_5_out, state3, not_17_out, not_18_out, state0, not_19_out, not_20_out);
  and and_6 (and_6_out, not_21_out, not_22_out, not_23_out, not_24_out, dir[0]);
  and and_7 (and_7_out, not_25_out, not_26_out, not_27_out, not_28_out, dir[1]);
  and and_8 (and_8_out, not_29_out, not_30_out, dir[1], dir[0]);
  and and_9 (and_9_out, not_31_out, state0, not_32_out, not_33_out);
  and and_10 (and_10_out, state2, not_34_out, not_35_out, not_36_out);
  and and_11 (and_11_out, state2, dir[1], dir[0]);
  and and_12 (and_12_out, state2, state0, not_37_out, not_38_out);
  and and_13 (and_13_out, state2, state1, not_39_out, dir[0]);
  and and_14 (and_14_out, state2, state1, not_40_out, dir[1]);
  and and_15 (and_15_out, not_41_out, not_42_out, not_43_out, dir[0]);
  and and_16 (and_16_out, not_44_out, not_45_out, not_46_out, dir[0]);
  and and_17 (and_17_out, not_47_out, not_48_out, not_49_out, not_50_out, dir[1]);
  and and_18 (and_18_out, not_51_out, state1, not_52_out, not_53_out, not_54_out);
  and and_19 (and_19_out, state2, state1, dir[0]);
  and and_20 (and_20_out, state2, state1, not_55_out, dir[1]);
  and and_21 (and_21_out, state3, not_56_out, not_57_out);
  and and_22 (and_22_out, not_58_out, not_59_out, not_60_out);
  and and_23 (and_23_out, not_61_out, state0, dir[1], dir[0]);
  and and_24 (and_24_out, not_62_out, state1, not_63_out, dir[1], dir[0]);
  and and_25 (and_25_out, state2, not_64_out);
  and and_26 (and_26_out, state2, state0, dir[1], dir[0]);
  and and_27 (and_27_out, state3, dir[1], dir[0]);
  or or_1 (out_5[3], and_1_out, and_2_out, and_3_out, and_4_out, and_5_out);
  or or_2 (out_5[2], and_6_out, and_7_out, and_8_out, and_9_out, and_10_out, and_11_out, and_12_out, and_13_out, and_14_out);
  or or_3 (out_5[1], and_15_out, and_16_out, and_17_out, and_18_out, and_19_out, and_20_out, and_21_out);
  or or_4 (out_5[0], and_22_out, and_23_out, and_24_out, and_25_out, and_26_out, and_27_out);
  Register #(.width(1)) register_1 (.D(out_5[3]), .Q(state3), .clk(in_2), .clr(reset));  // open: en
  Register #(.width(1)) register_2 (.D(out_5[2]), .Q(state2), .clk(in_2), .clr(reset));  // open: en
  Register #(.width(1)) register_3 (.D(out_5[1]), .Q(state1), .clk(in_2), .clr(reset));  // open: en
  Register #(.width(1)) register_4 (.D(out_5[0]), .Q(state0), .clk(in_2), .clr(reset));  // open: en
  // Probe on out_5[3]
  // Probe on out_5[2]
  // Probe on out_5[1]
  // Probe on out_5[0]
  not not_65 (not_65_out, out_5[3]);
  not not_66 (not_66_out, out_5[2]);
  and and_28 (and_28_out, not_65_out, not_66_out, out_5[1], out_5[0]);
  Comparator #(.width(4), .mode("unsigned")) comparator_1 (
    .a(out_5), .b(4'b0100), .gt(comparator_1_gt));  // open: eq, lt
  // Probe on out_5
  Multiplexer multiplexer_1 (.in0(and_28_out), .in1(1'b0), .out(arrive), .sel(reset));  // open: en
  Multiplexer multiplexer_2 (.in0(comparator_1_gt), .in1(1'b0), .out(hit), .sel(reset));  // open: en

  // Other names for the same wires on the sheet: clk = in_2; now0 = out_5[0]; now1 = out_5[1]; now2 = out_5[2];
  //   now3 = out_5[3]
endmodule
