// Logisim project test.circ as structural Verilog: 1 circuit, main circuit main
module main (
  input  in_1,
  output out_2,
  output out_3,
  output out_4
);

  wire clock_1_out;
  wire [1:0] rom_1_data;
  wire [4:0] counter_1_q;

  Counter #(.width(5), .max('h1f)) counter_1 (
    .Q(counter_1_q), .carry(out_4), .clk(clock_1_out), .clr(in_1));  // open: load, D, count
  Clock clock_1 (.out(clock_1_out));
  ROM #(.addrWidth(5), .dataWidth(2)) rom_1 (.addr(counter_1_q), .data(rom_1_data));  // open: sel

  // Notes on the sheet:
  //   contents of rom_1 (hex, n*v repeats v):
  //   0 3 0 4*3 1 1 2 0 0 2 3 1 2 3 1 2 3 2 2 0 2 1 0 3 3 2 0 0 3
endmodule
