// Logisim project CPU - 副本.circ as structural Verilog: 10 circuits, main circuit Adder
module Adder (
  input  [31:0] A,
  input  [31:0] B,
  output [31:0] sum
);

  Adder_part #(.width(32)) adder_1 (.a(A), .b(B), .out(sum));  // open: cin, cout
endmodule

module Registers (
  input  Clk,
  input  Reset,
  input  WE,
  input  [4:0] Read1,
  input  [4:0] Read2,
  input  [4:0] Write,
  input  [31:0] WriteDdta,
  output [31:0] RData1,
  output [31:0] RData2
);

  wire comparator_1_eq, in1, in2, in3, in4, in5, in6, in7, in8, in9, in10, in11, in12, in13, in14, in15,
       in16, in17, in18, in19, in20, in21, in22, in23, in24, in25, in26, in27, in28, in29, in30, in31, in32;
  wire [31:0] in, o1, o2, o3, o4, o5, o6, o7, o8, o9, o10, o11, o12, o13, o14, o15, o16, o17, o18, o19, o20,
       o21, o22, o23, o24, o25, o26, o27, o28, o29, o30, o31, o32;

  Demultiplexer #(.select(5)) demultiplexer_1 (
    .out0(in1), .out1(in2), .out2(in3), .out3(in4), .out4(in5), .out5(in6), .out6(in7), .out7(in8),
    .out8(in9), .out9(in10), .out10(in11), .out11(in12), .out12(in13), .out13(in14), .out14(in15),
    .out15(in16), .out16(in17), .out17(in18), .out18(in19), .out19(in20), .out20(in21), .out21(in22),
    .out22(in23), .out23(in24), .out24(in25), .out25(in26), .out26(in27), .out27(in28), .out28(in29),
    .out29(in30), .out30(in31), .out31(in32), .in(WE), .sel(Write));  // open: en
  Comparator #(.width(5)) comparator_1 (.a(Write), .b({5{1'b0}}), .eq(comparator_1_eq));  // open: gt, lt
  Multiplexer #(.width(32), .disabled(0)) multiplexer_1 (
    .in0(WriteDdta), .in1({32{1'b0}}), .out(in), .sel(comparator_1_eq));  // open: en
  Multiplexer #(.select(5), .width(32)) multiplexer_2 (
    .in0(o1), .in1(o2), .in2(o3), .in3(o4), .in4(o5), .in5(o6), .in6(o7), .in7(o8), .in8(o9), .in9(o10),
    .in10(o11), .in11(o12), .in12(o13), .in13(o14), .in14(o15), .in15(o16), .in16(o17), .in17(o18),
    .in18(o19), .in19(o20), .in20(o21), .in21(o22), .in22(o23), .in23(o24), .in24(o25), .in25(o26),
    .in26(o27), .in27(o28), .in28(o29), .in29(o30), .in30(o31), .in31(o32), .out(RData1), .sel(Read1));  // open: en
  // Probe on o9
  Register #(.width(32)) register_1 (.D(in), .en(in1), .Q(o1), .clk(Clk), .clr(Reset));
  Register #(.width(32)) register_2 (.D(in), .en(in9), .Q(o9), .clk(Clk), .clr(Reset));
  Register #(.width(32)) register_3 (.D(in), .en(in17), .Q(o17), .clk(Clk), .clr(Reset));
  Register #(.width(32)) register_4 (.D(in), .en(in25), .Q(o25), .clk(Clk), .clr(Reset));
  Multiplexer #(.select(5), .width(32)) multiplexer_3 (
    .in0(o1), .in1(o2), .in2(o3), .in3(o4), .in4(o5), .in5(o6), .in6(o7), .in7(o8), .in8(o9), .in9(o10),
    .in10(o11), .in11(o12), .in12(o13), .in13(o14), .in14(o15), .in15(o16), .in16(o17), .in17(o18),
    .in18(o19), .in19(o20), .in20(o21), .in21(o22), .in22(o23), .in23(o24), .in24(o25), .in25(o26),
    .in26(o27), .in27(o28), .in28(o29), .in29(o30), .in30(o31), .in31(o32), .out(RData2), .sel(Read2));  // open: en
  Register #(.width(32)) register_5 (.D(in), .en(in2), .Q(o2), .clk(Clk), .clr(Reset));
  Register #(.width(32)) register_6 (.D(in), .en(in10), .Q(o10), .clk(Clk), .clr(Reset));
  Register #(.width(32)) register_7 (.D(in), .en(in18), .Q(o18), .clk(Clk), .clr(Reset));
  Register #(.width(32)) register_8 (.D(in), .en(in26), .Q(o26), .clk(Clk), .clr(Reset));
  Register #(.width(32)) register_9 (.D(in), .en(in3), .Q(o3), .clk(Clk), .clr(Reset));
  Register #(.width(32)) register_10 (.D(in), .en(in11), .Q(o11), .clk(Clk), .clr(Reset));
  Register #(.width(32)) register_11 (.D(in), .en(in19), .Q(o19), .clk(Clk), .clr(Reset));
  Register #(.width(32)) register_12 (.D(in), .en(in27), .Q(o27), .clk(Clk), .clr(Reset));
  Register #(.width(32)) register_13 (.D(in), .en(in4), .Q(o4), .clk(Clk), .clr(Reset));
  Register #(.width(32)) register_14 (.D(in), .en(in12), .Q(o12), .clk(Clk), .clr(Reset));
  Register #(.width(32)) register_15 (.D(in), .en(in20), .Q(o20), .clk(Clk), .clr(Reset));
  Register #(.width(32)) register_16 (.D(in), .en(in28), .Q(o28), .clk(Clk), .clr(Reset));
  Register #(.width(32)) register_17 (.D(in), .en(in5), .Q(o5), .clk(Clk), .clr(Reset));
  Register #(.width(32)) register_18 (.D(in), .en(in13), .Q(o13), .clk(Clk), .clr(Reset));
  Register #(.width(32)) register_19 (.D(in), .en(in21), .Q(o21), .clk(Clk), .clr(Reset));
  Register #(.width(32)) register_20 (.D(in), .en(in29), .Q(o29), .clk(Clk), .clr(Reset));
  Register #(.width(32)) register_21 (.D(in), .en(in6), .Q(o6), .clk(Clk), .clr(Reset));
  Register #(.width(32)) register_22 (.D(in), .en(in14), .Q(o14), .clk(Clk), .clr(Reset));
  Register #(.width(32)) register_23 (.D(in), .en(in22), .Q(o22), .clk(Clk), .clr(Reset));
  Register #(.width(32)) register_24 (.D(in), .en(in30), .Q(o30), .clk(Clk), .clr(Reset));
  Register #(.width(32)) register_25 (.D(in), .en(in7), .Q(o7), .clk(Clk), .clr(Reset));
  Register #(.width(32)) register_26 (.D(in), .en(in15), .Q(o15), .clk(Clk), .clr(Reset));
  Register #(.width(32)) register_27 (.D(in), .en(in23), .Q(o23), .clk(Clk), .clr(Reset));
  Register #(.width(32)) register_28 (.D(in), .en(in31), .Q(o31), .clk(Clk), .clr(Reset));
  // Probe on o32
  Register #(.width(32)) register_29 (.D(in), .en(in8), .Q(o8), .clk(Clk), .clr(Reset));
  Register #(.width(32)) register_30 (.D(in), .en(in16), .Q(o16), .clk(Clk), .clr(Reset));
  Register #(.width(32)) register_31 (.D(in), .en(in24), .Q(o24), .clk(Clk), .clr(Reset));
  Register #(.width(32)) register_32 (.D(in), .en(in32), .Q(o32), .clk(Clk), .clr(Reset));

  // Other names for the same wires on the sheet: A1[4:0] = Read1; A2[4:0] = Read2; A3[4:0] = Write;
  //   RD1[31:0] = RData1; RD2[31:0] = RData2; WD[31:0] = WriteDdta
endmodule

module DataMemory (
  input  [4:0] Addr,
  input  [31:0] WD,
  input  WE,
  input  clk,
  input  reset,
  output [31:0] RD
);

  RAM #(.addrWidth(5), .dataWidth(32), .bus("separate")) ram_1 (
    .addr(Addr), .din(WD), .data(RD), .str(WE), .clk(clk), .clr(reset));  // open: sel, ld
endmodule

module IFU (
  input  Clk,
  input  Reset,
  input  [1:0] PCSrc,
  input  [31:0] Imm,
  output [31:0] Instruction,
  output [31:0] PC
);

  wire [31:0] adder_2_out, imm_t, multiplexer_1_out, register_1_q;

  Shifter #(.width(32)) shifter_1 (.in(Imm), .\dist (5'b00010), .out(imm_t));
  Register #(.width(32)) register_1 (.D(multiplexer_1_out), .Q(register_1_q), .clk(Clk), .clr(Reset));  // open: en
  // Probe on register_1_q
  Adder_part #(.width(32)) adder_1 (.a(register_1_q), .b(32'h4), .out(PC));  // open: cin, cout
  ROM #(.addrWidth(5), .dataWidth(32)) rom_1 (.addr(register_1_q[6:2]), .data(Instruction));  // open: sel
  Adder_part #(.width(32)) adder_2 (.a(PC), .b(imm_t), .out(adder_2_out));  // open: cin, cout
  Multiplexer #(.select(2), .width(32)) multiplexer_1 (
    .in0(PC), .in1(adder_2_out), .in2(Imm), .in3(Imm), .out(multiplexer_1_out), .sel(PCSrc));  // open: en
  // Probe on multiplexer_1_out

  // Other names for the same wires on the sheet: JImm[31:0] = Imm; PC_4[31:0] = PC

  // Notes on the sheet:
  //   contents of rom_1 (hex, n*v repeats v):
  //   34110020 34120000 34100000 12110006 ae500000 34080004 2489021 34080001 2088021 1000fff9
endmodule

// 1
module main (
  input  Reset,
  output [31:0] Instr,
  output RegWrite,
  output [4:0] RegAddr,
  output [31:0] RegData,
  output MemWrite,
  output [4:0] MemAddr,
  output [31:0] MemData
);

  wire ALUSrc, Branch, clk, JR, jump, Link, zero;
  wire [1:0] EXTctrl, MemToReg, PCSrc, RegDst;
  wire [2:0] ALUOp;
  wire [27:0] PC;
  wire [31:0] alu_1_result, datamemory_1_rd, imm32, multiplexer_1_out, multiplexer_3_out, R_Rs;
  wire [31:28] JImm;

  // Probe on ALUOp
  // Probe on Instr[25:21]
  // Probe on Instr[20:16]
  // Probe on EXTctrl
  // Probe on Instr[15:11]
  // Probe on PCSrc
  and and_1 (PCSrc[0], zero, Branch);
  or or_1 (PCSrc[1], jump, JR);
  Clock clock_1 (.out(clk));
  Multiplexer #(.select(2), .width(32)) multiplexer_1 (
    .in0(imm32), .in1({JImm, Instr[25:0], 2'b00}), .in2(R_Rs), .in3(R_Rs), .out(multiplexer_1_out),
    .sel({JR, jump}));  // open: en
  IFU ifu_1 (.Clk(clk), .Reset(Reset), .PCSrc(PCSrc), .Imm(multiplexer_1_out), .Instruction(Instr), .PC({JImm, PC}));
  // Probe on Instr[31:26]
  control control_1 (
    .Op(Instr[31:26]), .RegDst(RegDst), .ALUSrc(ALUSrc), .MemtoReg(MemToReg), .RegWrite(RegWrite),
    .MemWrite(MemWrite), .Branch(Branch), .ALUOp(ALUOp), .EXTctrl(EXTctrl), .Jump(jump), .Link(Link),
    .JR(JR), .Func(Instr[5:0]));
  Multiplexer #(.select(2), .width(5)) multiplexer_2 (
    .in0(Instr[20:16]), .in1(Instr[15:11]), .in2({5{1'b1}}), .in3({5{1'b1}}), .out(RegAddr), .sel(RegDst));  // open: en
  Ext ext_1 (.imm16(Instr[15:0]), .imm32(imm32), .EXTCtrl(EXTctrl));
  Registers registers_1 (
    .Read1(Instr[25:21]), .Read2(Instr[20:16]), .Write(RegAddr), .WriteDdta(RegData), .RData1(R_Rs),
    .RData2(MemData), .Clk(clk), .Reset(Reset), .WE(RegWrite));
  Multiplexer #(.width(32)) multiplexer_3 (
    .in0(MemData), .in1(imm32), .out(multiplexer_3_out), .sel(ALUSrc));  // open: en
  ALU alu_1 (
    .A(R_Rs), .B(multiplexer_3_out), .Zero(zero), .Result({alu_1_result[31:7], MemAddr, alu_1_result[1:0]}),
    .ALUOp(ALUOp), .shamt(Instr[10:6]));
  Multiplexer #(.select(2), .width(32)) multiplexer_4 (
    .in0({alu_1_result[31:7], MemAddr, alu_1_result[1:0]}), .in1(datamemory_1_rd), .in2({JImm, PC}),
    .in3({JImm, PC}), .out(RegData), .sel(MemToReg));  // open: en
  DataMemory datamemory_1 (.Addr(MemAddr), .WD(MemData), .RD(datamemory_1_rd), .WE(MemWrite), .clk(clk), .reset(Reset));

  // Other names for the same wires on the sheet: Op[5:0] = Instr[31:26]; Func[5:0] = Instr[5:0];
  //   imm16[15:0] = Instr[15:0]; JImm[27:2] = Instr[25:0]; shamt[4:0] = Instr[10:6]; Rd[4:0] = Instr[15:11];
  //   Rt[4:0] = Instr[20:16]; Rs[4:0] = Instr[25:21]; PC[31:28] = JImm; Waddr[4:0] = RegAddr; Wdata[31:0] = RegData;
  //   WE = MemWrite
endmodule

module Ext (
  input  [15:0] imm16,
  input  [1:0] EXTCtrl,
  output [31:0] imm32
);

  wire [31:0] bit_extender_1_out, bit_extender_2_out, bit_extender_3_out;

  assign bit_extender_1_out = {{16{1'b0}}, imm16};  // Bit_Extender bit_extender_1
  assign bit_extender_2_out = {{16{imm16[15]}}, imm16};  // Bit_Extender bit_extender_2
  assign bit_extender_3_out = {{16{1'b1}}, imm16};  // Bit_Extender bit_extender_3
  Multiplexer #(.select(2), .width(32)) multiplexer_1 (
    .in0(bit_extender_1_out), .in1(bit_extender_2_out), .in2({imm16, {16{1'b0}}}), .in3(bit_extender_3_out),
    .out(imm32), .sel(EXTCtrl));  // open: en
endmodule

module ALU (
  input  [2:0] ALUOp,
  input  [31:0] A,
  input  [31:0] B,
  input  [4:0] shamt,
  output Zero,
  output [31:0] Result
);

  wire [31:0] adder_1_out, and_1_out, or_1_out, shifter_1_out, subtractor_1_out;

  Shifter #(.width(32)) shifter_1 (.in(B), .\dist (shamt), .out(shifter_1_out));
  assign and_1_out = A & B;  // AND_Gate and_1, 32 bits wide
  assign or_1_out = A | B;  // OR_Gate or_1, 32 bits wide
  Subtractor #(.width(32)) subtractor_1 (.a(A), .b(B), .out(subtractor_1_out));  // open: bin, bout
  Adder_part #(.width(32)) adder_1 (.a(A), .b(B), .out(adder_1_out));  // open: cin, cout
  Multiplexer #(.select(3), .width(32)) multiplexer_1 (
    .in0(shifter_1_out), .in1(and_1_out), .in2(or_1_out), .in3(subtractor_1_out), .in4(adder_1_out),
    .in5({32{1'b0}}), .in6({32{1'b0}}), .in7({32{1'b0}}), .out(Result), .sel(ALUOp));  // open: en
  Comparator #(.width(32), .mode("unsigned")) comparator_1 (.a({32{1'b0}}), .b(Result), .eq(Zero));  // open: gt, lt

  // Other names for the same wires on the sheet: op[2:0] = ALUOp
endmodule

module control (
  input  [5:0] Op,
  input  [5:0] Func,
  output [1:0] RegDst,
  output ALUSrc,
  output [1:0] MemtoReg,
  output RegWrite,
  output MemWrite,
  output Branch,
  output [1:0] EXTctrl,
  output Jump,
  output Link,
  output JR,
  output [2:0] ALUOp
);

  wire addiu, addu, comparator_1_eq, comparator_2_eq, comparator_3_eq, comparator_4_eq, j, not_1_out,
       not_2_out, not_3_out, not_4_out, not_5_out, not_6_out, not_7_out, not_8_out, not_9_out, not_10_out,
       not_11_out, not_12_out, not_13_out, not_14_out, not_15_out, not_16_out, not_17_out, not_18_out,
       not_19_out, not_20_out, not_21_out, not_22_out, not_23_out, not_24_out, not_25_out, not_26_out,
       not_27_out, not_28_out, not_29_out, not_30_out, not_31_out, not_32_out, not_33_out, not_34_out,
       or_1_out, or_2_out, or_3_out, or_4_out, or_5_out, ori, sll, subu;

  Comparator #(.width(6)) comparator_1 (.a(Func), .b({6{1'b0}}), .eq(comparator_1_eq));  // open: gt, lt
  and and_1 (sll, comparator_1_eq, RegDst[0]);
  Comparator #(.width(6)) comparator_2 (.a(Func), .b(6'b001000), .eq(comparator_2_eq));  // open: gt, lt
  and and_2 (JR, comparator_2_eq, RegDst[0]);
  Comparator #(.width(6)) comparator_3 (.a(Func), .b(6'b100001), .eq(comparator_3_eq));  // open: gt, lt
  and and_3 (addu, comparator_3_eq, RegDst[0]);
  Comparator #(.width(6)) comparator_4 (.a(Func), .b(6'b100011), .eq(comparator_4_eq));  // open: gt, lt
  and and_4 (subu, comparator_4_eq, RegDst[0]);
  not not_1 (not_1_out, Op[5]);
  not not_2 (not_2_out, Op[1]);
  not not_3 (not_3_out, Op[4]);
  not not_4 (not_4_out, Op[2]);
  not not_5 (not_5_out, Op[3]);
  and and_5 (RegDst[0], not_1_out, not_3_out, not_5_out, not_4_out, not_2_out, not_7_out);
  not not_6 (not_6_out, Op[4]);
  not not_7 (not_7_out, Op[0]);
  not not_8 (not_8_out, Op[2]);
  not not_9 (not_9_out, Op[3]);
  and and_6 (MemtoReg[0], Op[5], not_6_out, not_9_out, not_8_out, Op[1], Op[0]);
  not not_10 (not_10_out, Op[4]);
  and and_7 (MemWrite, Op[5], not_10_out, Op[3], not_11_out, Op[1], Op[0]);
  or or_1 (or_1_out, MemtoReg[0], MemWrite);
  not not_11 (not_11_out, Op[2]);
  not not_12 (not_12_out, Op[5]);
  not not_13 (not_13_out, Op[3]);
  not not_14 (not_14_out, Op[1]);
  not not_15 (not_15_out, Op[4]);
  and and_8 (Branch, not_12_out, not_15_out, not_13_out, Op[2], not_14_out, not_18_out);
  not not_16 (not_16_out, Op[4]);
  not not_17 (not_17_out, Op[5]);
  not not_18 (not_18_out, Op[0]);
  not not_19 (not_19_out, Op[1]);
  and and_9 (ori, not_17_out, not_16_out, Op[3], Op[2], not_19_out, Op[0]);
  not not_20 (not_20_out, Op[4]);
  not not_21 (not_21_out, Op[5]);
  and and_10 (EXTctrl[1], not_21_out, not_20_out, Op[3], Op[2], Op[1], Op[0]);
  not not_22 (not_22_out, Op[5]);
  not not_23 (not_23_out, Op[2]);
  not not_24 (not_24_out, Op[1]);
  not not_25 (not_25_out, Op[4]);
  and and_11 (addiu, not_22_out, not_25_out, Op[3], not_23_out, not_24_out, Op[0]);
  not not_26 (not_26_out, Op[4]);
  not not_27 (not_27_out, Op[3]);
  not not_28 (not_28_out, Op[5]);
  not not_29 (not_29_out, Op[0]);
  not not_30 (not_30_out, Op[3]);
  and and_12 (j, not_28_out, not_26_out, not_27_out, not_30_out, Op[1], not_29_out);
  not not_31 (not_31_out, Op[3]);
  not not_32 (not_32_out, Op[2]);
  not not_33 (not_33_out, Op[4]);
  not not_34 (not_34_out, Op[5]);
  and and_13 (Link, not_34_out, not_33_out, not_31_out, not_32_out, Op[1], Op[0]);
  buf or_2 (or_2_out, 1'b0);  // OR_Gate
  buf or_3 (or_3_out, ori);  // OR_Gate
  or or_4 (or_4_out, subu, Branch);
  or or_5 (or_5_out, addu, addiu, or_1_out, EXTctrl[1]);
  or or_6 (ALUSrc, ori, MemtoReg[0], addiu, MemWrite, EXTctrl[1]);
  or or_7 (RegWrite, Link, ori, RegDst[0], MemtoReg[0], EXTctrl[1], addiu);
  or or_8 (EXTctrl[0], Branch, MemWrite, MemtoReg[0]);
  or or_9 (Jump, Link, j);
  Priority_Encoder priority_encoder_1 (
    .in0(sll), .in1(or_2_out), .in2(or_3_out), .in3(or_4_out), .in4(or_5_out), .out(ALUOp));  // open: in5, in6, in7, en_in, gs, en_out

  assign MemtoReg[1] = Link;
  assign RegDst[1] = Link;

  // Other names for the same wires on the sheet: beq = Branch; lui = EXTctrl[1]; lw = MemtoReg[0]; jal = Link;
  //   R = RegDst[0]; sw = MemWrite
endmodule

module ALUCtrl (
  input  [5:0] Func,
  input  [2:0] ALUtype,
  input  sll,
  output [3:0] ALUOp
);

  wire Add, Addu, And, not_1_out, not_2_out, not_3_out, not_4_out, not_5_out, not_6_out, not_7_out,
       not_8_out, not_9_out, not_10_out, not_11_out, not_12_out, not_13_out, not_14_out, not_15_out,
       not_16_out, not_17_out, not_18_out, not_19_out, not_20_out, not_21_out, not_22_out, not_23_out, Or,
       or_1_out, or_2_out, or_3_out, Sub, Subu;
  wire [1:0] priority_encoder_1_out;
  wire [3:0] ALUOp_t, R;

  not not_1 (not_1_out, Func[4]);
  not not_2 (not_2_out, Func[2]);
  not not_3 (not_3_out, Func[0]);
  not not_4 (not_4_out, Func[1]);
  not not_5 (not_5_out, Func[3]);
  and and_1 (Add, Func[5], not_1_out, not_5_out, not_2_out, not_4_out, not_3_out);
  not not_6 (not_6_out, Func[4]);
  not not_7 (not_7_out, Func[3]);
  not not_8 (not_8_out, Func[2]);
  and and_2 (Sub, Func[5], not_6_out, not_7_out, not_8_out, Func[1], not_10_out);
  Multiplexer #(.select(2), .width(4)) multiplexer_1 (
    .in0(4'b1000), .in1(4'b0100), .in2(R), .in3(4'b0000), .out(ALUOp_t), .sel(ALUtype[1:0]));  // open: en
  not not_9 (not_9_out, Func[4]);
  not not_10 (not_10_out, Func[0]);
  not not_11 (not_11_out, Func[1]);
  not not_12 (not_12_out, Func[3]);
  not not_13 (not_13_out, Func[0]);
  and and_3 (And, Func[5], not_9_out, not_12_out, Func[2], not_11_out, not_13_out);
  not not_14 (not_14_out, Func[3]);
  not not_15 (not_15_out, Func[4]);
  and and_4 (Or, Func[5], not_15_out, not_14_out, Func[2], not_16_out, Func[0]);
  not not_16 (not_16_out, Func[1]);
  not not_17 (not_17_out, Func[4]);
  not not_18 (not_18_out, Func[3]);
  not not_19 (not_19_out, Func[1]);
  not not_20 (not_20_out, Func[2]);
  and and_5 (Addu, Func[5], not_17_out, not_18_out, not_20_out, not_19_out, Func[0]);
  not not_21 (not_21_out, Func[4]);
  not not_22 (not_22_out, Func[2]);
  not not_23 (not_23_out, Func[3]);
  and and_6 (Subu, Func[5], not_21_out, not_23_out, not_22_out, Func[1], Func[0]);
  or or_1 (or_1_out, Sub, Subu);
  or or_2 (or_2_out, Add, Addu);
  Priority_Encoder #(.select(2)) priority_encoder_1 (
    .in0(Or), .in1(And), .in2(or_1_out), .in3(or_2_out), .out(priority_encoder_1_out));  // open: gs, en_out, en_in
  // Probe on priority_encoder_1_out
  // Probe on R
  Multiplexer #(.select(2), .width(4)) multiplexer_2 (
    .in0(4'b0010), .in1(4'b0001), .in2(4'b0100), .in3(4'b1000), .out(R), .sel(priority_encoder_1_out));  // open: en
  Multiplexer #(.width(4)) multiplexer_3 (.in0(ALUOp_t), .in1(4'b0000), .out(ALUOp), .sel(or_3_out));  // open: en
  or or_3 (or_3_out, sll, ALUtype[2]);

  // Other names for the same wires on the sheet: I = ALUtype[2]
endmodule

module test (
  input  reset,
  input  PCSrc,
  input  [31:0] imm,
  output [31:0] Instr,
  output RegWrite,
  output [4:0] RegAddr,
  output out_7,
  output [31:0] RegData,
  output MemWrite,
  output [4:0] MemAddr,
  output [31:0] MemData,
  output [31:0] instruction,
  output [31:0] out_13
);

  wire clk, clock_1_out, comparator_1_gt;
  wire [7:0] counter_1_q;
  wire [31:0] adder_2_out, imm_t, multiplexer_1_out, PC_4, register_1_q;

  Clock clock_1 (.out(clock_1_out));
  Counter counter_1 (.Q(counter_1_q), .carry(out_7), .clk(clock_1_out));  // open: load, D, count, clr
  Clock clock_2 (.out(clk));
  Comparator comparator_1 (.a(8'h4), .b(counter_1_q), .gt(comparator_1_gt));  // open: eq, lt
  main main_1 (
    .Reset(comparator_1_gt), .Instr(Instr), .RegWrite(RegWrite), .RegAddr(RegAddr), .RegData(RegData),
    .MemWrite(MemWrite), .MemAddr(MemAddr), .MemData(MemData));
  Shifter #(.width(32)) shifter_1 (.in(imm), .\dist (5'b00010), .out(imm_t));
  Register #(.width(32)) register_1 (.D(multiplexer_1_out), .Q(register_1_q), .clk(clk), .clr(reset));  // open: en
  Adder_part #(.width(32)) adder_1 (.a(register_1_q), .b(32'h4), .out(PC_4));  // open: cin, cout
  ROM #(.addrWidth(5), .dataWidth(32)) rom_1 (.addr(register_1_q[6:2]), .data(instruction));  // open: sel
  Adder_part #(.width(32)) adder_2 (.a(PC_4), .b(imm_t), .out(adder_2_out));  // open: cin, cout
  Subtractor #(.width(32)) subtractor_1 (.a({32{1'b0}}), .b({32{1'b1}}), .out(out_13));  // open: bin, bout
  Multiplexer #(.width(32)) multiplexer_1 (
    .in0(PC_4), .in1(adder_2_out), .out(multiplexer_1_out), .sel(PCSrc));  // open: en

  // Notes on the sheet:
  //   contents of rom_1 (hex, n*v repeats v):
  //   25080001 3c0a0001 8c090000 25290001 1109fffe 3c0a0001 1294821 1084021
endmodule
