// Logisim project 5.circ as structural Verilog
module main (
  input  [1:0] in_1,
  input  [3:0] in_2,
  input  in_3
);

  wire decoder_1_out0, decoder_2_out0, decoder_2_out1, decoder_2_out2, decoder_2_out3, decoder_2_out4,
       decoder_2_out5, decoder_2_out6, decoder_2_out7, decoder_2_out8, decoder_2_out9, decoder_2_out10,
       decoder_2_out11, decoder_2_out12, decoder_2_out13, decoder_2_out14, decoder_2_out15, nand_1_out,
       nand_2_out, nand_3_out, nand_4_out, nand_5_out, nand_6_out, nand_7_out, nand_8_out, nand_9_out,
       nand_10_out, nand_11_out, nand_12_out, nand_13_out, nand_14_out, nand_15_out, nand_16_out;
  wire [9:0] A9_A0, DB0_DB3, DB4_DB7;

  Decoder #(.select(2)) decoder_1 (.out0(decoder_1_out0), .sel(in_1));  // open: out1, out2, out3, en
  Decoder #(.select(4)) decoder_2 (
    .out0(decoder_2_out0), .out1(decoder_2_out1), .out2(decoder_2_out2), .out3(decoder_2_out3),
    .out4(decoder_2_out4), .out5(decoder_2_out5), .out6(decoder_2_out6), .out7(decoder_2_out7),
    .out8(decoder_2_out8), .out9(decoder_2_out9), .out10(decoder_2_out10), .out11(decoder_2_out11),
    .out12(decoder_2_out12), .out13(decoder_2_out13), .out14(decoder_2_out14), .out15(decoder_2_out15),
    .sel(in_2));  // open: en
  nand nand_1 (nand_1_out, decoder_1_out0, decoder_2_out0);
  nand nand_2 (nand_2_out, decoder_1_out0, decoder_2_out1);
  nand nand_3 (nand_3_out, decoder_1_out0, decoder_2_out2);
  nand nand_4 (nand_4_out, decoder_1_out0, decoder_2_out3);
  nand nand_5 (nand_5_out, decoder_1_out0, decoder_2_out4);
  nand nand_6 (nand_6_out, decoder_1_out0, decoder_2_out5);
  nand nand_7 (nand_7_out, decoder_1_out0, decoder_2_out6);
  nand nand_8 (nand_8_out, decoder_1_out0, decoder_2_out7);
  nand nand_9 (nand_9_out, decoder_1_out0, decoder_2_out8);
  nand nand_10 (nand_10_out, decoder_1_out0, decoder_2_out9);
  nand nand_11 (nand_11_out, decoder_1_out0, decoder_2_out10);
  nand nand_12 (nand_12_out, decoder_1_out0, decoder_2_out11);
  nand nand_13 (nand_13_out, decoder_1_out0, decoder_2_out12);
  nand nand_14 (nand_14_out, decoder_1_out0, decoder_2_out13);
  nand nand_15 (nand_15_out, decoder_1_out0, decoder_2_out14);
  nand nand_16 (nand_16_out, decoder_1_out0, decoder_2_out15);
  _1_4 u_1_4_1 (.out_4(DB0_DB3), .in_3(A9_A0), .in_1(nand_1_out), .in_2(in_3));
  _1_4 u_1_4_2 (.out_4(DB0_DB3), .in_3(A9_A0), .in_1(nand_2_out), .in_2(in_3));
  _1_4 u_1_4_3 (.out_4(DB0_DB3), .in_3(A9_A0), .in_1(nand_3_out), .in_2(in_3));
  _1_4 u_1_4_4 (.out_4(DB0_DB3), .in_3(A9_A0), .in_1(nand_4_out), .in_2(in_3));
  _1_4 u_1_4_5 (.out_4(DB0_DB3), .in_3(A9_A0), .in_1(nand_5_out), .in_2(in_3));
  _1_4 u_1_4_6 (.out_4(DB0_DB3), .in_3(A9_A0), .in_1(nand_6_out), .in_2(in_3));
  _1_4 u_1_4_7 (.out_4(DB0_DB3), .in_3(A9_A0), .in_1(nand_7_out), .in_2(in_3));
  _1_4 u_1_4_8 (.out_4(DB0_DB3), .in_3(A9_A0), .in_1(nand_8_out), .in_2(in_3));
  _1_4 u_1_4_9 (.out_4(DB0_DB3), .in_3(A9_A0), .in_1(nand_9_out), .in_2(in_3));
  _1_4 u_1_4_10 (.out_4(DB0_DB3), .in_3(A9_A0), .in_1(nand_10_out), .in_2(in_3));
  _1_4 u_1_4_11 (.out_4(DB0_DB3), .in_3(A9_A0), .in_1(nand_11_out), .in_2(in_3));
  _1_4 u_1_4_12 (.out_4(DB0_DB3), .in_3(A9_A0), .in_1(nand_12_out), .in_2(in_3));
  _1_4 u_1_4_13 (.out_4(DB0_DB3), .in_3(A9_A0), .in_1(nand_13_out), .in_2(in_3));
  _1_4 u_1_4_14 (.out_4(DB0_DB3), .in_3(A9_A0), .in_1(nand_14_out), .in_2(in_3));
  _1_4 u_1_4_15 (.out_4(DB0_DB3), .in_3(A9_A0), .in_1(nand_15_out), .in_2(in_3));
  _1_4 u_1_4_16 (.out_4(DB0_DB3), .in_3(A9_A0), .in_1(nand_16_out), .in_2(in_3));
  _1_4 u_1_4_17 (.out_4(DB4_DB7), .in_3(A9_A0), .in_1(nand_1_out), .in_2(in_3));
  _1_4 u_1_4_18 (.out_4(DB4_DB7), .in_3(A9_A0), .in_1(nand_2_out), .in_2(in_3));
  _1_4 u_1_4_19 (.out_4(DB4_DB7), .in_3(A9_A0), .in_1(nand_3_out), .in_2(in_3));
  _1_4 u_1_4_20 (.out_4(DB4_DB7), .in_3(A9_A0), .in_1(nand_4_out), .in_2(in_3));
  _1_4 u_1_4_21 (.out_4(DB4_DB7), .in_3(A9_A0), .in_1(nand_5_out), .in_2(in_3));
  _1_4 u_1_4_22 (.out_4(DB4_DB7), .in_3(A9_A0), .in_1(nand_6_out), .in_2(in_3));
  _1_4 u_1_4_23 (.out_4(DB4_DB7), .in_3(A9_A0), .in_1(nand_7_out), .in_2(in_3));
  _1_4 u_1_4_24 (.out_4(DB4_DB7), .in_3(A9_A0), .in_1(nand_8_out), .in_2(in_3));
  _1_4 u_1_4_25 (.out_4(DB4_DB7), .in_3(A9_A0), .in_1(nand_9_out), .in_2(in_3));
  _1_4 u_1_4_26 (.out_4(DB4_DB7), .in_3(A9_A0), .in_1(nand_10_out), .in_2(in_3));
  _1_4 u_1_4_27 (.out_4(DB4_DB7), .in_3(A9_A0), .in_1(nand_11_out), .in_2(in_3));
  _1_4 u_1_4_28 (.out_4(DB4_DB7), .in_3(A9_A0), .in_1(nand_12_out), .in_2(in_3));
  _1_4 u_1_4_29 (.out_4(DB4_DB7), .in_3(A9_A0), .in_1(nand_13_out), .in_2(in_3));
  _1_4 u_1_4_30 (.out_4(DB4_DB7), .in_3(A9_A0), .in_1(nand_14_out), .in_2(in_3));
  _1_4 u_1_4_31 (.out_4(DB4_DB7), .in_3(A9_A0), .in_1(nand_15_out), .in_2(in_3));
  _1_4 u_1_4_32 (.out_4(DB4_DB7), .in_3(A9_A0), .in_1(nand_16_out), .in_2(in_3));

  // Other names for the same wires on the sheet: A13_A10[3:0] = in_2; A15_A14[1:0] = in_1; nWE = in_3
endmodule

module _1_4 (
  input  in_1,
  input  in_2,
  input  [9:0] in_3,
  output [9:0] out_4
);


  assign out_4 = in_3;
endmodule

module _8_8 (
  input  in_1,
  input  in_2,
  input  [9:0] in_3,
  output [9:0] out_4
);


  assign out_4 = in_3;
endmodule
