// Logisim project D锁存器.circ as structural Verilog: 2 circuits, main circuit main
module main (
  input  clk,
  input  D,
  output Q,
  output out_4
);

  wire not_1_out;

  not not_1 (not_1_out, D);
  and and_1 (Q, clk, not_1_out);
  and and_2 (out_4, clk, D);
endmodule

module \D触发器  (
  input  in_1,
  input  in_2,
  output out_3,
  output out_4
);

  wire main_1_q, not_1_out;

  not not_1 (not_1_out, in_1);
  main main_1 (.D(in_2), .clk(not_1_out), .Q(main_1_q));  // open: out_4
  main main_2 (.D(main_1_q), .clk(in_1), .Q(out_3), .out_4(out_4));
endmodule
