// Logisim project count.circ as structural Verilog: 1 circuit, main circuit main
module main (
  input  in_1,
  input  [7:0] in_2,
  input  in_3,
  output [7:0] out_4
);

  wire clock_1_out;

  Clock clock_1 (.out(clock_1_out));
  Counter counter_1 (.load(in_1), .D(in_2), .count(in_3), .Q(out_4), .clk(clock_1_out));  // open: carry, clr
endmodule
