// Logisim project fib.circ as structural Verilog: 1 circuit, main circuit main
module main (
  input  [2:0] in_1,
  input  in_2,
  input  in_3,
  output [3:0] out_4
);

  wire and_1_out, clock_1_out, comparator_1_gt, comparator_2_eq, comparator_2_gt, or_1_out;
  wire [3:0] init, multiplexer_1_out, multiplexer_2_out, register_1_q, register_2_q;
  wire [6:0] counter_1_q, counter_2_q;

  Counter #(.width(7), .max('h7f)) counter_1 (.Q(counter_1_q));  // open: load, D, count, carry, clk, clr
  Counter #(.width(7), .max('h7f)) counter_2 (
    .load(1'b0), .count(1'b1), .Q(counter_2_q), .clk(clock_1_out), .clr(in_2));  // open: D, carry
  Clock clock_1 (.out(clock_1_out));
  // Probe on init
  Adder #(.width(4)) adder_1 (.a(register_1_q), .b(register_2_q), .out(init));  // open: cin, cout
  Comparator #(.width(7), .mode("unsigned")) comparator_1 (
    .a(counter_1_q), .b(7'b0000001), .gt(comparator_1_gt));  // open: eq, lt
  // Probe on register_1_q
  Multiplexer #(.width(4)) multiplexer_1 (
    .in0(4'b0001), .in1(init), .out(multiplexer_1_out), .sel(and_1_out));  // open: en
  and and_1 (and_1_out, comparator_1_gt, 1'b1);
  // Probe on counter_2_q[2:0]
  Register #(.width(4)) register_1 (.D(multiplexer_1_out), .Q(register_1_q), .clk(clock_1_out));  // open: en, clr
  // Probe on register_2_q
  Comparator #(.width(3), .mode("unsigned")) comparator_2 (
    .a(in_1), .b(counter_2_q[2:0]), .gt(comparator_2_gt), .eq(comparator_2_eq));  // open: lt
  Register #(.width(4)) register_2 (.D(register_1_q), .Q(register_2_q), .clk(clock_1_out));  // open: en, clr
  Multiplexer #(.width(4)) multiplexer_2 (
    .in0(4'b0000), .in1(register_2_q), .out(multiplexer_2_out), .sel(comparator_2_eq), .en(in_3));
  or or_1 (or_1_out, comparator_2_eq, comparator_2_gt);
  // Probe on multiplexer_2_out
  Counter #(.width(4), .max('hf)) counter_3 (
    .load(or_1_out), .D(multiplexer_2_out), .count(1'b0), .Q(out_4), .clk(clock_1_out));  // open: carry, clr
endmodule
