// Logisim project init.circ as structural Verilog: 1 circuit, main circuit main
module main (
  input  in_1,
  output out_2
);

  wire and_1_out, clock_1_out, comparator_1_gt, multiplexer_1_out;
  wire [6:0] counter_1_q;

  Clock clock_1 (.out(clock_1_out));
  Counter #(.width(7), .max('h7f)) counter_1 (.Q(counter_1_q));  // open: load, D, count, carry, clk, clr
  Comparator #(.width(7), .mode("unsigned")) comparator_1 (
    .a(counter_1_q), .b(7'b0000001), .gt(comparator_1_gt));  // open: eq, lt
  Multiplexer multiplexer_1 (.in0(1'b1), .in1(in_1), .out(multiplexer_1_out), .sel(and_1_out));  // open: en
  and and_1 (and_1_out, comparator_1_gt, 1'b1);
  Register #(.width(1)) register_1 (.D(multiplexer_1_out), .Q(out_2));  // open: en, clk, clr
endmodule
