// Logisim project mod5.circ as structural Verilog: 2 circuits, main circuit mod5
module mod5 (
  input  in,
  output s0,
  output s1,
  output s2,
  output s3,
  output s4
);

  wire and_1_out, and_2_out, and_3_out, and_4_out, and_5_out, and_6_out, clock_1_out, not_1_out, not_2_out,
       not_3_out, not_4_out, not_5_out, not_6_out, not_7_out, not_8_out, register_1_q, register_2_q;
  wire [1:0] or_2_out;

  not not_1 (not_1_out, register_1_q);
  not not_2 (not_2_out, register_2_q);
  not not_3 (not_3_out, in);
  not not_4 (not_4_out, register_1_q);
  not not_5 (not_5_out, in);
  not not_6 (not_6_out, register_2_q);
  not not_7 (not_7_out, register_1_q);
  not not_8 (not_8_out, register_2_q);
  and and_1 (and_1_out, not_1_out, register_2_q);
  and and_2 (and_2_out, register_1_q, not_2_out);
  Clock clock_1 (.out(clock_1_out));
  and and_3 (and_3_out, not_3_out, not_4_out, register_2_q);
  and and_4 (and_4_out, not_5_out, register_1_q, not_6_out);
  and and_5 (and_5_out, in, not_7_out, not_8_out);
  and and_6 (and_6_out, in, register_1_q, register_2_q);
  or or_1 (or_2_out[1], and_1_out, and_2_out);
  Register #(.width(1)) register_1 (.D(or_2_out[1]), .Q(register_1_q), .clk(clock_1_out));  // open: en, clr
  Register #(.width(1)) register_2 (.D(or_2_out[0]), .Q(register_2_q), .clk(clock_1_out));  // open: en, clr
  or or_2 (or_2_out[0], and_3_out, and_4_out, and_5_out, and_6_out);
  Demultiplexer #(.select(2)) demultiplexer_1 (
    .out0(s1), .out1(s2), .out2(s3), .out3(s4), .in(1'b1), .sel(or_2_out));  // open: en

  assign s0 = 1'b0;
endmodule

module test (
  input  in_1,
  output out_2,
  output out_3,
  output out_4,
  output out_5,
  output out_6,
  output out_7
);

  wire clock_1_out, rom_1_data;
  wire [3:0] counter_1_q;

  Counter #(.width(4), .max('hf)) counter_1 (
    .Q(counter_1_q), .carry(out_7), .clk(clock_1_out), .clr(in_1));  // open: load, D, count
  Clock clock_1 (.out(clock_1_out));
  // Probe on rom_1_data
  ROM #(.addrWidth(4), .dataWidth(1)) rom_1 (.addr(counter_1_q), .data(rom_1_data));  // open: sel
  mod5 mod5_1 (.in(rom_1_data), .s0(out_2), .s1(out_3), .s2(out_4), .s3(out_5), .s4(out_6));

  // Notes on the sheet:
  //   contents of rom_1 (hex, n*v repeats v):
  //   0 1 0 0 1 0 0 1 0 0 1 0 0 1
endmodule
