// Logisim project rs锁存器.circ as structural Verilog: 1 circuit, main circuit main
module main (
  input  in_1,
  input  in_2,
  input  in_3,
  input  in_4,
  output out_5,
  output out_6,
  output out_7,
  output out_8
);

  wire and_1_out, and_2_out, not_1_out, not_2_out, or_1_out, or_2_out;

  not not_1 (not_1_out, in_3);
  not not_2 (not_2_out, in_4);
  or or_1 (or_1_out, in_1, out_6);
  or or_2 (or_2_out, out_5, in_2);
  and and_1 (and_1_out, not_1_out, not_1_out, out_8);
  and and_2 (and_2_out, out_7, not_2_out);
  not not_3 (out_5, or_1_out);
  not not_4 (out_6, or_2_out);
  not not_5 (out_7, and_1_out);
  not not_6 (out_8, and_2_out);
endmodule
