// Logisim project sort.circ as structural Verilog: 3 circuits, main circuit 4bit_swap
module _4bit_swap (
  input  [3:0] in_1,
  input  [3:0] in_2,
  input  in_3,
  output [3:0] out_4,
  output [3:0] out_5
);

  _1bit_swap u_1bit_swap_1 (.i1(in_1[0]), .i2(in_2[0]), .s(in_3), .o1(out_4[0]), .o2(out_5[0]));
  _1bit_swap u_1bit_swap_2 (.i1(in_1[1]), .i2(in_2[1]), .s(in_3), .o1(out_4[1]), .o2(out_5[1]));
  _1bit_swap u_1bit_swap_3 (.i1(in_1[2]), .i2(in_2[2]), .s(in_3), .o1(out_4[2]), .o2(out_5[2]));
  _1bit_swap u_1bit_swap_4 (.i1(in_1[3]), .i2(in_2[3]), .s(in_3), .o1(out_4[3]), .o2(out_5[3]));
endmodule

module _1bit_swap (
  input  i1,
  input  i2,
  input  s,
  output o1,
  output o2
);

  wire and_1_out, and_2_out, and_3_out, and_4_out, not_1_out, not_2_out;

  not not_1 (not_1_out, s);
  not not_2 (not_2_out, s);
  and and_1 (and_1_out, i2, s);
  and and_2 (and_2_out, i1, not_1_out);
  and and_3 (and_3_out, i2, not_2_out);
  and and_4 (and_4_out, i1, s);
  or or_1 (o1, and_1_out, and_2_out);
  or or_2 (o2, and_3_out, and_4_out);
endmodule

module _4bit_sort (
  input  [3:0] d,
  input  [3:0] c,
  input  [3:0] b,
  input  [3:0] a,
  output [3:0] out_5,
  output [3:0] out_6,
  output [3:0] out_7,
  output [3:0] out_8
);

  wire comparator_1_gt, comparator_2_gt, comparator_3_gt, comparator_4_gt, comparator_5_gt, comparator_6_gt;
  wire [3:0] n4bit_swap_1_out_4, n4bit_swap_1_out_5, n4bit_swap_2_out_4, n4bit_swap_2_out_5,
       n4bit_swap_3_out_4, n4bit_swap_3_out_5, n4bit_swap_4_out_4, n4bit_swap_6_out_4;

  Comparator #(.width(4), .mode("unsigned")) comparator_1 (.a(b), .b(a), .gt(comparator_1_gt));  // open: eq, lt
  // Probe on n4bit_swap_1_out_5
  _4bit_swap u_4bit_swap_1 (
    .in_1(b), .in_2(a), .in_3(comparator_1_gt), .out_4(n4bit_swap_1_out_4), .out_5(n4bit_swap_1_out_5));
  Comparator #(.width(4), .mode("unsigned")) comparator_2 (
    .a(c), .b(n4bit_swap_1_out_5), .gt(comparator_2_gt));  // open: eq, lt
  _4bit_swap u_4bit_swap_2 (
    .in_1(c), .in_2(n4bit_swap_1_out_5), .in_3(comparator_2_gt), .out_4(n4bit_swap_2_out_4),
    .out_5(n4bit_swap_2_out_5));
  // Probe on n4bit_swap_2_out_5
  Comparator #(.width(4), .mode("unsigned")) comparator_3 (
    .a(n4bit_swap_2_out_4), .b(n4bit_swap_1_out_4), .gt(comparator_3_gt));  // open: eq, lt
  // Probe on n4bit_swap_3_out_4
  _4bit_swap u_4bit_swap_3 (
    .in_1(n4bit_swap_2_out_4), .in_2(n4bit_swap_1_out_4), .in_3(comparator_3_gt), .out_4(n4bit_swap_3_out_4),
    .out_5(n4bit_swap_3_out_5));
  Comparator #(.width(4), .mode("unsigned")) comparator_4 (
    .a(d), .b(n4bit_swap_2_out_5), .gt(comparator_4_gt));  // open: eq, lt
  // Probe on n4bit_swap_3_out_5
  // Probe on n4bit_swap_4_out_4
  _4bit_swap u_4bit_swap_4 (
    .in_1(d), .in_2(n4bit_swap_2_out_5), .in_3(comparator_4_gt), .out_4(n4bit_swap_4_out_4), .out_5(out_8));
  // Probe on out_8
  Comparator #(.width(4), .mode("unsigned")) comparator_5 (
    .a(n4bit_swap_6_out_4), .b(n4bit_swap_3_out_4), .gt(comparator_5_gt));  // open: eq, lt
  Comparator #(.width(4), .mode("unsigned")) comparator_6 (
    .a(n4bit_swap_4_out_4), .b(n4bit_swap_3_out_5), .gt(comparator_6_gt));  // open: eq, lt
  _4bit_swap u_4bit_swap_5 (
    .in_1(n4bit_swap_6_out_4), .in_2(n4bit_swap_3_out_4), .in_3(comparator_5_gt), .out_4(out_5), .out_5(out_6));
  _4bit_swap u_4bit_swap_6 (
    .in_1(n4bit_swap_4_out_4), .in_2(n4bit_swap_3_out_5), .in_3(comparator_6_gt), .out_4(n4bit_swap_6_out_4),
    .out_5(out_7));
endmodule
