// Logisim project test1.circ as structural Verilog: 1 circuit, main circuit swap
module swap (
  input  i1,
  input  i2,
  input  s,
  output o1,
  output o2
);

  wire and_1_out, and_2_out, and_3_out, and_4_out, not_1_out, not_2_out;

  not not_1 (not_1_out, s);
  not not_2 (not_2_out, s);
  and and_1 (and_1_out, i2, s);
  and and_2 (and_2_out, i1, not_1_out);
  and and_3 (and_3_out, i2, not_2_out);
  and and_4 (and_4_out, i1, s);
  or or_1 (o1, and_1_out, and_2_out);
  or or_2 (o2, and_3_out, and_4_out);
endmodule
