// Logisim project 一位全加器.circ as structural Verilog: 1 circuit, main circuit main
module main (
  input  A,
  input  in_2,
  input  in_3,
  input  [5:0] in_4,
  output out_5,
  output out_6,
  output [2:0] out_7
);

  wire and_1_out, and_2_out, xor_1_out;

  // Probe on in_4[2:0]
  xor xor_1 (xor_1_out, A, in_2);
  // Probe on in_3
  // Probe on in_4[5:3]
  xor xor_2 (out_5, xor_1_out, in_3);
  and and_1 (and_1_out, in_3, xor_1_out);
  and and_2 (and_2_out, A, in_2);
  or or_1 (out_6, and_1_out, and_2_out);
  assign out_7 = ~(in_4[2:0] ^ in_4[5:3]);  // XNOR_Gate xnor_1, 3 bits wide
  // Probe on out_7

  // Other names for the same wires on the sheet: xx = A
endmodule
