// Logisim project 多位多路选择器.circ as structural Verilog: 1 circuit, main circuit main
module main (
  input  [3:0] in_1,
  input  [3:0] in_2,
  input  [3:0] in_3,
  input  [3:0] in_4,
  input  in_5,
  input  [1:0] in_6,
  input  in_7,
  input  [1:0] in_8,
  input  [15:0] in_9,
  input  in_10,
  input  in_11,
  output [3:0] out_12,
  output out_13,
  output out_14,
  output out_15,
  output out_16,
  output [15:0] out_17,
  output [15:0] out_18
);

  wire undriven, undriven_3;
  wire [1:0] undriven_2;

  // Probe on out_17
  Demultiplexer #(.width(16)) demultiplexer_1 (.out0(out_17), .out1(out_18), .in(in_9), .sel(undriven), .en(in_10));
  Multiplexer #(.select(2), .width(4)) multiplexer_1 (
    .in0(in_1), .in1(in_2), .in2(in_3), .in3(in_4), .out(out_12), .sel(in_6), .en(undriven_3));
  Decoder #(.select(2), .enable("false")) decoder_1 (
    .out0(out_13), .out1(out_14), .out2(out_15), .out3(out_16), .sel(undriven_2));
endmodule
