// Logisim project 多路选择器....circ as structural Verilog: 1 circuit, main circuit main
module main (
  input  in_1,
  input  in_2,
  input  in_3,
  input  in_4,
  input  in_5,
  input  in_6,
  input  in_7,
  input  in_8,
  input  in_9,
  output out_10,
  output out_11,
  output out_12,
  output out_13,
  output out_14
);

  Multiplexer multiplexer_1 (.in0(in_1), .in1(in_2), .out(out_10), .sel(in_3), .en(in_4));
  Demultiplexer demultiplexer_1 (.out0(out_11), .out1(out_12), .in(in_5), .sel(in_7), .en(in_6));
  Decoder decoder_1 (.out0(out_13), .out1(out_14), .sel(in_9), .en(in_8));
endmodule
