// Logisim project 寄存器.circ as structural Verilog: 1 circuit, main circuit mod5
module mod5 (
  input  A,
  output s0,
  output s1,
  output s2,
  output s3,
  output s4
);

  wire and_1_out, and_2_out, and_3_out, and_4_out, and_5_out, and_6_out, not_1_out, not_2_out, not_3_out,
       not_4_out, not_5_out, not_6_out, not_7_out, not_8_out, not_9_out, not_10_out, register_1_q,
       register_2_q;
  wire [1:0] or_2_out;

  not not_1 (not_1_out, register_1_q);
  not not_2 (not_2_out, register_2_q);
  not not_3 (not_3_out, register_1_q);
  not not_4 (not_4_out, register_2_q);
  not not_5 (not_5_out, register_1_q);
  not not_6 (not_6_out, A);
  not not_7 (not_7_out, register_2_q);
  not not_8 (not_8_out, A);
  not not_9 (not_9_out, A);
  and and_1 (and_1_out, not_1_out, register_2_q);
  and and_2 (and_2_out, register_1_q, not_2_out);
  and and_3 (and_3_out, not_3_out, not_4_out, A);
  and and_4 (and_4_out, not_5_out, register_2_q, not_6_out);
  and and_5 (and_5_out, register_1_q, not_7_out, not_8_out);
  and and_6 (and_6_out, register_1_q, register_2_q, A);
  and and_7 (s0, A, not_9_out);
  or or_1 (or_2_out[1], and_1_out, and_2_out);
  or or_2 (or_2_out[0], and_3_out, and_4_out, and_5_out, and_6_out);
  Register #(.width(1)) register_1 (.D(or_2_out[1]), .Q(register_1_q));  // open: en, clk, clr
  Register #(.width(1)) register_2 (.D(or_2_out[0]), .Q(register_2_q));  // open: en, clk, clr
  not not_10 (not_10_out, s0);
  Demultiplexer #(.select(2)) demultiplexer_1 (
    .out0(s1), .out1(s2), .out2(s3), .out3(s4), .in(not_10_out), .sel(or_2_out));  // open: en
  // Probe on or_2_out
endmodule
